# Fritzing sketch SuperCam (saved by Fritzing 0.9.3b)

parts:
  A4988 = Pololu A4988 [package=SO16]
  WeMos_D1_Mini1 = WeMos D1 Mini
  A4988_2 = Pololu A4988 [package=SO16]
  A3144 = PNP-Transistor [package="TO92 [THT]"]
  R1 = Resistor [tolerance=±5% resistance=10k package=THT]

nets:
  N1: A4988.ENABLE, WeMos_D1_Mini1.D8
  N2: A4988.RESET, A4988.SLEEP
  N3: A4988.STEP, WeMos_D1_Mini1.D7
  N4: A4988.DIR, WeMos_D1_Mini1.D6
  GND: A4988.GND, WeMos_D1_Mini1.G, A4988_2.GND, A3144.B
  N5: A4988.VMOT, A4988_2.VMOT
  N6: WeMos_D1_Mini1.5V, A3144.E, R1.Pin_1
  N7: WeMos_D1_Mini1.A0, A3144.C, R1.Pin_0
  N8: WeMos_D1_Mini1.D0, A4988_2.STEP
  N9: WeMos_D1_Mini1.D3, A4988_2.DIR
  N10: WeMos_D1_Mini1.D5, A4988_2.ENABLE
  N11: A4988_2.RESET, A4988_2.SLEEP

notes:
  I2C
  Step
  Ena
  Dir
  Stepper 1
  Stepper 2
  Mars Rover 2020
  SuperCam
