# Fritzing sketch SuperCam_v2 (saved by Fritzing 0.9.3b)

parts:
  A4988 = Pololu A4988 [package=SO16]
  A4988_2 = Pololu A4988 [package=SO16]
  A3144 = PNP-Transistor [package="TO92 [THT]"]
  Composant1 = BluePill
  R1 = Resistor [tolerance=±5% resistance=10k package=THT]  # not connected

nets:
  N1: A4988.ENABLE, Composant1.A5
  VDD: A4988.MS1, A4988.MS2, A4988.MS3, A4988.VDD, A4988_2.VDD, A3144.E, Composant1.5V
  N2: A4988.RESET, A4988.SLEEP
  N3: A4988.STEP, Composant1.A4
  N4: A4988.DIR, Composant1.A3
  GND: A4988.GND, A4988_2.GND, A3144.B, Composant1.GND3
  N5: A4988.VMOT, A4988_2.VMOT
  N6: A4988_2.ENABLE, Composant1.A2
  N7: A4988_2.RESET, A4988_2.SLEEP
  N8: A4988_2.STEP, Composant1.A1
  N9: A4988_2.DIR, Composant1.A0
  N10: A3144.C, Composant1.A10

notes:
  I2C
  Step
  Ena
  Dir
  Stepper 1
  Stepper 2
  Mars Rover 2020
  SuperCam
  SDL
  SDA
  5V
  12V
  (bas)
  (haut)
  Micro stepping uniquement sur un moteur
  Courant max en 12 V (pour un moteur) : 0,3A
  Correspond à ~ 0.5 A par phase (1A total pour le moteur)
  hall effect sensor
