# Fritzing sketch TEST_Schema_2_Moteurs_Encodeurs (saved by Fritzing 0.9.3b)

parts:
  Composant1 = BluePill
  S1 = H-Bridge with L298N
  Composant2 = FTDI Basic Programmer
  Motor1 = Motor Encoder Pololu
  Motor2 = Motor Encoder Pololu
  S2 = Round Pushbutton
  S3 = Round Pushbutton

nets:
  N1: Composant1.A1, S1.IN1
  N2: Composant1.A3, S1.IN4
  N3: Composant1.A4, S1.IN3
  N4: Composant1.A6, Motor1.Yellow
  N5: Composant1.A7, Motor1.White
  N6: Composant1.B0, Motor2.Yellow
  GND: Composant1.GND, S1.GND
  N7: Composant1.3V31, Motor2.Blue
  GND3: Composant1.GND3, Composant2.GND, S2.leg0, S3.leg0
  5V: Composant1.5V, S1.5V, Composant2.POWER
  N8: Composant1.B9, S1.ENB
  N9: Composant1.B8, S1.ENA
  N10: Composant1.A10, Composant2.TXO
  N11: Composant1.A9, Composant2.RXI
  N12: Composant1.B13, S3.leg1
  N13: Composant1.B12, S2.leg1
  N14: Composant1.B1, Motor2.White
  N15: Composant1.A2, S1.IN2

notes:
  Test  -  STM32f103
  FTDI  -  YP-05
  stm32f103

custom parts:
  H-Bridge with L298N: h-bridge
  Motor Encoder Pololu: Pololu 37D mm Metal Gearmotors with Encoder https://www.pololu.com/category/116/37d-mm-metal-gearmotors
  Motor Encoder Pololu: Pololu 37D mm Metal Gearmotors with Encoder https://www.pololu.com/category/116/37d-mm-metal-gearmotors
