# Fritzing sketch Untitled Sketch (saved by Fritzing 0.9.3b)

parts:
  Pololu_A1 = Pololu A4988 [package=SO16]
  WeMos_D1_Mini1 = WeMos D1 Mini

nets:
  N1: Pololu_A1.STEP, WeMos_D1_Mini1.D5
  N2: Pololu_A1.DIR, WeMos_D1_Mini1.D6
  N3: Pololu_A1.GND, WeMos_D1_Mini1.G
  VDD: Pololu_A1.VDD, WeMos_D1_Mini1.5V
